# Fritzing sketch Schematic (saved by Fritzing 0.9.3b)
circuit board: 8.46667cm x 5.64444cm
breadboards: 1

parts:
  Controllerboard = Arduino Uno (Rev3)
  Battery = DC Power [voltage=7.4]
  Servo_1 = Basic Servo
  Servo_3 = Basic Servo
  Servo_4 = Basic Servo
  Servo_2 = Basic Servo

nets:
  N1: Controllerboard.D10_PWM/SS, Servo_3.pulse
  N2: Controllerboard.D11_PWM/MOSI, Servo_4.pulse
  GND: Controllerboard.GND, Battery.V-, Servo_1.gnd, Servo_3.gnd, Servo_4.gnd, Servo_2.gnd
  N3: Controllerboard.D3_PWM, Servo_1.pulse
  N4: Controllerboard.D5_PWM, Servo_2.pulse
  VCC: Controllerboard.VIN, Battery.V+, Servo_1.vcc, Servo_3.vcc, Servo_4.vcc, Servo_2.vcc
